# Fritzing sketch openHARMONIE (saved by Fritzing 0.9.6b)
perfboards: 1

parts:
  Raspberry_Pi_Zero_W = Raspberry Pi Zero
  IR_LED_1 = LEDs [package=led10mm]
  IR_LED_2 = LEDs [package=led10mm]
  2N2222 = NPN-Transistor [package="TO92 [THT]"]
  R3 = Resistor [tolerance=±5% resistance=22 package="0603 [SMD]"]
  R2 = Resistor [tolerance=±5% resistance=10 package="0603 [SMD]"]
  VS1838B = TSOP312.., 314.. [package=THT]
  R1 = Resistor [tolerance=±5% resistance=1k package="0805 [SMD]"]
  IR_LED_3 = LEDs [package=led10mm]

nets:
  N1: Raspberry_Pi_Zero_W.pin_2, R2.Pin_1, VS1838B.Vs
  N2: Raspberry_Pi_Zero_W.pin_6, Raspberry_Pi_Zero_W.pin_9, Raspberry_Pi_Zero_W.pin_25, 2N2222.E, VS1838B.GND
  N3: Raspberry_Pi_Zero_W.pin_11, VS1838B.Data
  N4: Raspberry_Pi_Zero_W.pin_12, R1.Pin_1
  N5: IR_LED_1.C, IR_LED_2.A
  N6: IR_LED_1.A, R3.Pin_0
  N7: IR_LED_2.C, IR_LED_3.A
  N8: 2N2222.B, R1.Pin_0
  N9: 2N2222.C, IR_LED_3.C
  N10: R3.Pin_1, R2.Pin_0
